# Fritzing sketch Wiring diagram (saved by Fritzing 0.9.6b)
breadboards: 1

parts:
  Part3 = Arduino Uno (Rev3)
  Part4 = Adafruit AT42QT1010 Standalone Momentary Capacitive Touch Sensor [part_number="Adafruit #1374"]
  Driver2 = 28BYJ-48 Driver Module [part_number=ULN2003 package=THT]
  SM2 = 28BYJ-48 Stepper Motor [part_number=28BYJ-48]
  Driver3 = 28BYJ-48 Driver Module [part_number=ULN2003 package=THT]
  SM3 = 28BYJ-48 Stepper Motor [part_number=28BYJ-48]  # not connected

nets:
  N1: Part3.A0, Part4.OUT
  N2: Part3.D8, Driver2.IN4, Driver3.IN1
  N3: Part3.D9_PWM, Driver2.IN3, Driver3.IN2
  N4: Part3.D10_PWM/SS, Driver2.IN2, Driver3.IN3
  N5: Part3.D11_PWM/MOSI, Driver2.IN1, Driver3.IN4
  5V: Part3.5V, Part4.VDD, Driver3.Vmotor
  GND: Part3.GND, Part4.GND, Driver2.GND, Driver2.Vmotor, Driver3.GND
  N6: Driver2.blue-pin, SM2.blue-pin
  N7: Driver2.pink-pin, SM2.pink-pin
  N8: Driver2.yellow-pin, SM2.yellow-pin
  N9: Driver2.orange-pin, SM2.orange-pin
  N10: Driver2.red-pin, SM2.red-pin

custom parts:
  Adafruit AT42QT1010 Standalone Momentary Capacitive Touch Sensor: This breakout board is the simplest way to create a project with a single "momentary" capacitive touch sensor. No microcontroller is required here - just power with 1.8 to 5.5VDC and touch the pad to activate the sensor. When a capacitive load is detected (e.g. a person touches the sensor-pad area) the red LED lights up and the output pin goes high. You can also solder a wire to the middle pad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
  28BYJ-48 Driver Module: ULN2003 Driver Module for the 28BYJ-48 Unipolar Stepper Motor LED A - Blue wire - Bottom coil left LED B - Pink wire - Top coil left LED C - Yellow wire - Bottom coil right LED D - Orange wire - Top coil right Common rail - red Connector pins: blue - pink - yellow - orange - red Control pins - IN1 to IN4 Power pins - GND & Vmotor (5-12V) On/Off jumper (if removed, power to motor is cut).
  28BYJ-48 Stepper Motor: Unipolar Stepper Motor 28BYJ-48 Top coil - pink & orange Bottom coil - blue & yellow Common rail - red Connector pins: blue - pink - yellow - orange - red
